# Fritzing sketch gps_neo6m (saved by Fritzing 0.9.4)

parts:
  GY-NEO6MV2 = SUP500F [package=sup500f]
  Raspberry_Pi_1 = Raspberry Pi 3 [part_number=RPI-3-V1.2]

nets:
  N1: GY-NEO6MV2.RX-I, Raspberry_Pi_1.GND
  N2: GY-NEO6MV2.TX-O, Raspberry_Pi_1.GPIO15
  VCC: GY-NEO6MV2.VCC, Raspberry_Pi_1.5V

notes:
  GND: Black
  TXD: Yellow (GPIO15)
  RXD: (unused)
  VCC: Red 5V
